# Fritzing sketch countdown (saved by Fritzing 0.9.3b)
circuit board: 2.25cm x 5cm
breadboards: 1

parts:
  U4 = SO16 [chip_label=TLC5916 package=SO]
  U6 = IC, SIP package, 7 pins [chip_label=IC]
  R1 = Resistor [tolerance=±5% resistance=220 package=THT]
  U5 = IC, SIP package, 7 pins [chip_label=IC]
  D1 = Resistor [tolerance=±5% resistance=220 package=THT]
  J1 = female pin header, 4 pins [form="♀ (female)"]
  J5 = female pin header, 4 pins [form="♀ (female)"]
  J6 = female pin header, 4 pins [form="♀ (female)"]
  J4 = female pin header, 4 pins [form="♀ (female)"]

nets:
  N1: U4.1, R1.Pin_0, J1.pin4, J5.pin4
  N2: U4.2, J4.pin2
  N3: U4.3, J6.pin1, J4.pin1
  N4: U4.4, J6.pin3, J4.pin3
  N5: U4.5, U6.pin6
  N6: U4.6, U6.pin4
  N7: U4.7, U6.pin3
  N8: U4.8, D1.Pin_1
  N9: U4.9, U6.pin1
  N10: U4.10, U5.pin7
  N11: U4.11, U5.pin2
  N12: U4.12, U5.pin1
  N13: U4.13, J6.pin4, J4.pin4
  N14: U4.14, J6.pin2
  N15: U4.15, R1.Pin_1
  N16: U4.16, J1.pin1, J5.pin1
  N17: U6.pin2, D1.Pin_0
  N18: U6.pin7, J1.pin3, J5.pin3

notes:
  Vdd
  GND
  Vled
  NC
  SDI
  LE
  OE
  CLK
  TLC5916
  D1
  +
  -
